// Logisim project Processador.circ as structural Verilog: 5 circuits, main circuit main
module main (
  input  CLEAR
);

  wire and_1_out, Branch, CLOCK, Igual, Jump, MemRead, MemToReg, MemWrite, not_1_out, or_1_out, RegDst,
       RegWrite, ULASrc;
  wire [1:0] ULAOp;
  wire [2:0] Controle_ULA_ulactrl, multiplexer_3_out, opcode, rs, rt;
  wire [2:2] rd;
  wire [7:0] adder_1_out, address_imm, banco_de_registradores_1_read_data_1, Conteudo_RT, multiplexer_1_out,
       multiplexer_2_out, multiplexer_4_out, PC, \Saída_Memoria , \Saída_ULA , \Saída_ULA_t , ULA_address;

  Adder adder_1 (.a(8'h1), .b(PC), .out(adder_1_out));  // open: cin, cout
  or or_1 (or_1_out, Jump, and_1_out);
  and and_1 (and_1_out, Branch, Igual);
  Multiplexer #(.width(8), .enable("false")) multiplexer_1 (
    .in0(adder_1_out), .in1(address_imm), .out(multiplexer_1_out), .sel(or_1_out));
  Register u_PC (.D(multiplexer_1_out), .Q(PC), .clk(CLOCK), .clr(CLEAR));  // open: en
  Clock clock_1 (.out(CLOCK));
  ROM #(.dataWidth(18)) rom_1 (.addr(PC), .data({opcode, rs, rt, rd[2], address_imm}));  // open: sel
  Unidade_de_Controle unidade_de_controle_1 (
    .opcode(opcode), .RegDst(RegDst), .RegWrite(RegWrite), .ULASrc(ULASrc), .MemWrite(MemWrite),
    .MemRead(MemRead), .MemToReg(MemToReg), .Branch(Branch), .Jump(Jump), .ULAOp(ULAOp));
  Multiplexer #(.width(8), .enable("false")) multiplexer_2 (
    .in0(\Saída_Memoria ), .in1(\Saída_ULA ), .out(multiplexer_2_out), .sel(MemToReg));
  Multiplexer #(.width(3), .enable("false")) multiplexer_3 (
    .in0(rt), .in1({rd[2], address_imm[7:6]}), .out(multiplexer_3_out), .sel(RegDst));
  not not_1 (not_1_out, CLOCK);
  Banco_de_Registradores banco_de_registradores_1 (
    .Read_register_1(rs), .Read_register_2(rt), .Write_Data(multiplexer_2_out),
    .Write_register(multiplexer_3_out), .RegWrite(RegWrite),
    .Read_data_1(banco_de_registradores_1_read_data_1), .Read_data_2(Conteudo_RT), .CLOCK(CLOCK),
    .CLEAR(CLEAR));
  RAM #(.bus("separate")) ram_1 (
    .addr(ULA_address), .din(Conteudo_RT), .data(\Saída_Memoria ), .str(MemWrite), .clk(not_1_out),
    .ld(MemRead), .clr(CLEAR));  // open: sel
  Multiplexer #(.width(8), .enable("false")) multiplexer_4 (
    .in0(Conteudo_RT), .in1(address_imm), .out(multiplexer_4_out), .sel(ULASrc));
  Controle_ULA Controle_ULA (.Funct(address_imm[2:0]), .ULAOp(ULAOp), .ULACtrl(Controle_ULA_ulactrl));
  ULA ula_1 (
    .\Função (Controle_ULA_ulactrl), .Shamt(address_imm[5:3]), .A(banco_de_registradores_1_read_data_1),
    .B(multiplexer_4_out), .Resultado(\Saída_ULA_t ), .Igual(Igual));

  // Other names for the same wires on the sheet: funct[2:0] = address_imm[2:0]; rd[1:0] = address_imm[7:6];
  //   shamt[2:0] = address_imm[5:3]
endmodule

// Registradores
module Banco_de_Registradores (
  input  [2:0] Read_register_1,
  input  [2:0] Read_register_2,
  input  [7:0] Write_Data,
  input  [2:0] Write_register,
  input  RegWrite,
  input  CLOCK,
  input  CLEAR,
  output [7:0] Read_data_1,
  output [7:0] Read_data_2
);

  wire WE0, WE1, WE2, WE3, WE4, WE5, WE6, WE7;
  wire [7:0] Reg0, Reg1, Reg2, Reg3, Reg4, Reg5, Reg6, Reg7, WriteReg0, WriteReg1, WriteReg2, WriteReg3,
       WriteReg4, WriteReg5, WriteReg6, WriteReg7;

  Demultiplexer #(.select(3), .width(8), .enable("false")) demultiplexer_1 (
    .out0(WriteReg0), .out1(WriteReg1), .out2(WriteReg2), .out3(WriteReg3), .out4(WriteReg4),
    .out5(WriteReg5), .out6(WriteReg6), .out7(WriteReg7), .in(Write_Data), .sel(Write_register));
  Demultiplexer #(.select(3), .enable("false")) demultiplexer_2 (
    .out0(WE0), .out1(WE1), .out2(WE2), .out3(WE3), .out4(WE4), .out5(WE5), .out6(WE6), .out7(WE7),
    .in(RegWrite), .sel(Write_register));
  Register u_Reg0 (.D(WriteReg0), .en(WE0), .Q(Reg0), .clk(CLOCK), .clr(CLEAR));
  Register u_Reg1 (.D(WriteReg1), .en(WE1), .Q(Reg1), .clk(CLOCK), .clr(CLEAR));
  Register u_Reg2 (.D(WriteReg2), .en(WE2), .Q(Reg2), .clk(CLOCK), .clr(CLEAR));
  Register u_Reg3 (.D(WriteReg3), .en(WE3), .Q(Reg3), .clk(CLOCK), .clr(CLEAR));
  Register u_Reg4 (.D(WriteReg4), .en(WE4), .Q(Reg4), .clk(CLOCK), .clr(CLEAR));
  Register u_Reg5 (.D(WriteReg5), .en(WE5), .Q(Reg5), .clk(CLOCK), .clr(CLEAR));
  Register u_Reg6 (.D(WriteReg6), .en(WE6), .Q(Reg6), .clk(CLOCK), .clr(CLEAR));
  Register u_Reg7 (.D(WriteReg7), .en(WE7), .Q(Reg7), .clk(CLOCK), .clr(CLEAR));
  Multiplexer #(.select(3), .width(8), .enable("false")) multiplexer_1 (
    .in0(Reg0), .in1(Reg1), .in2(Reg2), .in3(Reg3), .in4(Reg4), .in5(Reg5), .in6(Reg6), .in7(Reg7),
    .out(Read_data_1), .sel(Read_register_1));
  Multiplexer #(.select(3), .width(8), .enable("false")) multiplexer_2 (
    .in0(Reg0), .in1(Reg1), .in2(Reg2), .in3(Reg3), .in4(Reg4), .in5(Reg5), .in6(Reg6), .in7(Reg7),
    .out(Read_data_2), .sel(Read_register_2));

  // Other names for the same wires on the sheet: Read1[2:0] = Read_register_1; Read2[2:0] = Read_register_2
endmodule

module ULA (
  input  [2:0] \Função ,
  input  [2:0] Shamt,
  input  [7:0] A,
  input  [7:0] B,
  output [7:0] Resultado,
  output Igual
);

  wire comparator_1_lt;
  wire [7:0] CompA, CompB, DivA, DivB, MultA, MultB, NegA, RComp, RDiv, RMult, RNegA, RShiftDirA, RShiftEsqA,
       RSoma, RSub, ShiftDirA, ShiftEsqA, SomaA, SomaB, SubA, SubB;

  Demultiplexer #(.select(3), .width(8), .enable("false")) demultiplexer_1 (
    .out0(SomaA), .out1(SubA), .out2(MultA), .out3(DivA), .out4(NegA), .out5(CompA), .out6(ShiftEsqA),
    .out7(ShiftDirA), .in(A), .sel(\Função ));
  Demultiplexer #(.select(3), .width(8), .enable("false")) demultiplexer_2 (
    .out0(SomaB), .out1(SubB), .out2(MultB), .out3(DivB), .out5(CompB), .in(B), .sel(\Função ));  // open: out4, out6, out7
  Adder adder_1 (.a(SomaA), .b(SomaB), .out(RSoma));  // open: cin, cout
  Subtractor subtractor_1 (.a(SubA), .b(SubB), .out(RSub));  // open: bin, bout
  Multiplier multiplier_1 (.a(MultA), .b(MultB), .out(RMult));  // open: cin, cout
  Divider divider_1 (.a(DivA), .b(DivB), .out(RDiv));  // open: upper, rem
  Negator negator_1 (.in(NegA), .out(RNegA));
  Comparator comparator_1 (.a(CompA), .b(CompB), .eq(Igual), .lt(comparator_1_lt));  // open: gt
  Shifter shifter_1 (.in(ShiftEsqA), .\dist (Shamt), .out(RShiftEsqA));
  Shifter #(.shift("lr")) shifter_2 (.in(ShiftDirA), .\dist (Shamt), .out(RShiftDirA));
  assign RComp = {{7{1'b0}}, comparator_1_lt};  // Bit_Extender bit_extender_1
  Multiplexer #(.select(3), .width(8), .enable("false")) multiplexer_1 (
    .in0(RSoma), .in1(RSub), .in2(RMult), .in3(RDiv), .in4(RNegA), .in5(RComp), .in6(RShiftEsqA),
    .in7(RShiftDirA), .out(Resultado), .sel(\Função ));
endmodule

module Unidade_de_Controle (
  input  [2:0] opcode,
  output RegDst,
  output RegWrite,
  output ULASrc,
  output MemWrite,
  output MemRead,
  output MemToReg,
  output Branch,
  output Jump,
  output [1:0] ULAOp
);

  wire and_1_out, and_4_out, and_5_out, and_8_out, and_9_out, nor_2_out;

  nor nor_1 (RegDst, opcode[0], opcode[1], opcode[2]);
  nor nor_2 (nor_2_out, opcode[1], opcode[2]);
  or or_1 (RegWrite, nor_2_out, and_1_out);
  and and_1 (and_1_out, ~opcode[0], ~opcode[1], opcode[2]);  // AND_Gate
  ExactlyOne xor_1 (.out(ULASrc), .in0(opcode[0]), .in1(opcode[1]), .in2(opcode[2]));
  and and_2 (MemWrite, ~opcode[0], opcode[1], ~opcode[2]);  // AND_Gate
  and and_3 (MemRead, opcode[0], ~opcode[1], ~opcode[2]);  // AND_Gate
  and and_4 (and_4_out, ~opcode[0], ~opcode[1], ~opcode[2]);  // AND_Gate
  or or_2 (MemToReg, and_4_out, and_5_out);
  and and_5 (and_5_out, ~opcode[0], ~opcode[1], opcode[2]);  // AND_Gate
  and and_6 (Branch, opcode[0], opcode[1], ~opcode[2]);  // AND_Gate
  and and_7 (Jump, opcode[0], opcode[1], opcode[2]);
  and and_8 (and_8_out, opcode[0], opcode[1], ~opcode[2]);  // AND_Gate
  or or_3 (ULAOp[0], and_8_out, and_9_out);
  and and_9 (and_9_out, ~opcode[0], ~opcode[1], opcode[2]);  // AND_Gate
  and and_10 (ULAOp[1], ~opcode[0], ~opcode[1]);  // AND_Gate
endmodule

module Controle_ULA (
  input  [2:0] Funct,
  input  [1:0] ULAOp,
  output [2:0] ULACtrl
);

  Multiplexer #(.select(2), .width(3), .enable("false")) multiplexer_1 (
    .in0(3'b000), .in1(3'b101), .in2(Funct), .in3(3'b000), .out(ULACtrl), .sel(ULAOp));
endmodule
